# Fritzing sketch Scheme (saved by Fritzing 0.9.5d)
breadboards: 1

parts:
  Компонент1 = Arduino Nano (Rev3.0) (ICSP)
  S5 = Pushbutton [package="[THT]"]

nets:
  N1: Компонент1.GND, S5.Pin_1, S5.Pin_2
  N2: Компонент1.D5, S5.Pin_3, S5.Pin_4
